# Fritzing sketch Sedna (saved by Fritzing 0.9.3b)
circuit board: 7.13807cm x 3.57063cm
breadboards: 1

parts:
  BME680 = Adafruit BME680
  S1 = Pushbutton [package="[THT]"]
  R2 = Resistor [tolerance=±5% resistance=220 package=THT]
  Xenon = Particle Xenon

nets:
  3.3V: BME680.VIN, R2.Pin_1, Xenon.3.3V
  GND: BME680.GND, S1.Pin_1, S1.Pin_2, Xenon.GND
  N1: BME680.SCK/SCL, Xenon.SCL
  N2: BME680.SDI/SDA, Xenon.SDA
  N3: S1.Pin_3, S1.Pin_4, R2.Pin_0, Xenon.D2

custom parts:
  Particle Xenon: The Boron LTE is a powerful LTE CAT-M1 enabled development kit that can act as either a standalone cellular device or LTE enabled gateway, repeater, or endpoint for a Particle Mesh networks. Equipped with the Nordic nRF52840 and u-blox SARA 410 processors, the Boron has built-in battery charging circuitry which makes it easier to connect a Li-Po battery and 20 mixed signal GPIOs to interface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
